# Fritzing sketch ORDER12881 (saved by Fritzing 0.9.3b)
breadboards: 1

parts:
  Part1 = RFID-RC522-v2
  U2 = Mini-360 DC-DC Buck converter [package=THT]
  Mod1 = KY-019 5V Relay Module [package="Breakout board"]
  U6 = NodeMCU V3.0
  VALVE1 = Plastic Solenoid Valve
  VCC1 = 4 x AAA Battery Mount

nets:
  N1: Part1.SDA, U6.D8
  N2: Part1.SCK, U6.D5
  N3: Part1.MOSI, U6.D7
  N4: Part1.MISO, U6.D6
  GND: Part1.GND, U2.OUT-, Mod1.-, U6.GND
  N5: Part1.RST, U6.D1
  3.3V: Part1.3.3V, U6.3V3
  N6: U2.IN-, Mod1.NC, VCC1.+
  N7: U2.IN+, VALVE1.no_name_yet#1, VCC1.-
  N8: U2.OUT+, Mod1.+, U6.Vin
  N9: Mod1.S, U6.D4
  N10: Mod1.Common, VALVE1.no_name_yet#2

custom parts:
  RFID-RC522-v2: A simple China made RFID-RC522 Reader; do check the pin labels, as this is a MFRC522 based clone.
  Mini-360 DC-DC Buck converter: Mini-360 DC-DC Buck converter. Tiny buck step down voltage converter, input voltage 4.75 to 23V output 1 to 17V adjustable. Available from ebay and the like.
  KY-019 5V Relay Module: KY-019 5V Relay module, used to control AC circuits. (Special thanks to vanepp for fixing the PCB holes and other errors)
  NodeMCU V3.0: NodeMcu V3 Lua WIFI Development Board
